// Logisim project HW 2_circuit 2.circ as structural Verilog: 1 circuit, main circuit main
module main (
  input  B,
  input  D,
  input  B_2,
  input  A,
  input  C,
  output B_nD___BA___CD
);

  wire and_1_out, and_2_out, and_3_out, not_1_out;

  not not_1 (not_1_out, D);
  and and_1 (and_1_out, B, not_1_out);
  and and_2 (and_2_out, B_2, A);
  and and_3 (and_3_out, C, D);
  or or_1 (B_nD___BA___CD, and_1_out, and_2_out, and_3_out);

  // Notes on the sheet:
  //   !D
  //   B!D
  //   BA
  //   CD
endmodule
