// Logisim project HW 2_circuit 3a.circ as structural Verilog: 1 circuit, main circuit main
module main (
  input  A,
  input  B,
  output A_nB
);

  wire nB_out;

  not nB (nB_out, B);
  and and_1 (A_nB, A, nB_out);
endmodule
