// Logisim project HW 2_circuit 3b.circ as structural Verilog: 1 circuit, main circuit main
module main (
  input  A,
  input  C,
  output A_nC
);

  wire nC_out;

  not nC (nC_out, C);
  buf and_1 (A_nC, nC_out);  // AND_Gate
endmodule
