// Logisim project Exercise2a.circ as structural Verilog: 1 circuit, main circuit main
module main (
  input  A,
  input  B,
  input  C,
  output X
);

  wire AND_2_out, AND_out, NOT_out;

  not NOT (NOT_out, A);
  and AND (AND_out, A, B);
  and AND_2 (AND_2_out, C, NOT_out);
  or OR (X, AND_out, AND_2_out);

  // Notes on the sheet:
  //   A'
endmodule
