// Logisim project Exercise2b.circ as structural Verilog: 1 circuit, main circuit main
module main (
  input  A,
  input  B,
  input  C,
  input  D,
  output ABC_D
);

  wire AND_2_out, AND_out;

  and AND (AND_out, A, B);
  and AND_2 (AND_2_out, AND_out, C);
  or OR (ABC_D, AND_2_out, D);

  // Notes on the sheet:
  //   AB
  //   ABC
  //   D
endmodule
