// Logisim project Exercise3.circ as structural Verilog: 1 circuit, main circuit main
module main (
  input  A,
  input  B,
  input  C,
  input  D,
  output X
);

  wire OR_2_out, OR_out;

  or OR (OR_out, A, B);
  or OR_2 (OR_2_out, C, D);
  and AND (X, OR_out, OR_2_out);

  // Notes on the sheet:
  //   A+B
  //   C+D
endmodule
