// Logisim project question 4.circ as structural Verilog: 1 circuit, main circuit main
module main (
  input  A,
  input  B,
  input  C,
  input  D,
  output out_5
);

  wire A___B_out, C___D_out, nA___B___D_out, nA_out;

  or A___B (A___B_out, A, B);
  not nA (nA_out, A);
  or C___D (C___D_out, C, D);
  or nA___B___D (nA___B___D_out, nA_out, B, D);
  and and_1 (out_5, A___B_out, nA___B___D_out, C___D_out);

  // Notes on the sheet:
  //   (A+B) (C+D) (!A+B+D)
endmodule
