// Logisim project 1st complement.circ as structural Verilog: 1 circuit, main circuit main
module main (
  input  A,
  input  B,
  input  C,
  output nA,
  output nB,
  output nC
);

  not not_1 (nA, A);
  not not_2 (nB, B);
  not not_3 (nC, C);
endmodule
