// Logisim project 2nd complement.circ as structural Verilog: 1 circuit, main circuit main
module main (
  input  A,
  input  B,
  input  C,
  output nA_nB_nC,
  output out_5,
  output B_nC___nBC,
  output C_2
);

  wire A_nB_nC_out, B_nC_out, nAB_out, nAC_out, nBC_out, not_1_out, not_2_out, not_3_out, not_4_out,
       not_5_out, not_6_out, not_7_out, not_8_out;

  not not_1 (not_1_out, A);
  not not_2 (not_2_out, B);
  not not_3 (not_3_out, C);
  not not_4 (not_4_out, C);
  not not_5 (not_5_out, B);
  not not_6 (not_6_out, A);
  not not_7 (not_7_out, B);
  not not_8 (not_8_out, C);
  and nAB (nAB_out, not_1_out, B);
  and nAC (nAC_out, not_1_out, C);
  and A_nB_nC (A_nB_nC_out, A, not_2_out, not_3_out);
  and B_nC (B_nC_out, B, not_4_out);
  and nBC (nBC_out, not_5_out, C);
  or or_1 (nA_nB_nC, not_6_out, not_7_out, not_8_out);
  or or_2 (out_5, nAB_out, nAC_out, A_nB_nC_out);
  or or_3 (B_nC___nBC, B_nC_out, nBC_out);

  assign C_2 = C;

  // Notes on the sheet:
  //   !AB + !AC + A!B!C
endmodule
