// Logisim project hw3_ex1.circ as structural Verilog: 1 circuit, main circuit main
module main (
  input  A0,
  input  A1,
  input  A2,
  input  in_4,
  input  in_5,
  output F4,
  output F3,
  output F2,
  output F1,
  output F0
);


  assign F0 = in_5;
  assign F1 = in_4;
  assign F2 = A0;
  assign F3 = A1;
  assign F4 = A2;

  // Notes on the sheet:
  //   F4: pull=up
endmodule
