// Logisim project hw3_ex2.circ as structural Verilog: 1 circuit, main circuit main
module main (
  input  E,
  input  A2,
  input  A1,
  input  A0,
  output D0,
  output D1,
  output D2,
  output D3,
  output D4,
  output D5,
  output D6,
  output D7,
  output D0_2,
  output D1_2,
  output D2_2,
  output D3_2,
  output D4_2,
  output D5_2,
  output D6_2,
  output D7_2
);

  wire not_1_out;

  Decoder #(.select(3)) decoder_1 (
    .out0(D0), .out1(D1), .out2(D2), .out3(D3), .out4(D4), .out5(D5), .out6(D6), .out7(D7),
    .sel({A2, A1, A0}), .en(not_1_out));
  not not_1 (not_1_out, E);
  Decoder #(.select(3)) decoder_2 (
    .out0(D0_2), .out1(D1_2), .out2(D2_2), .out3(D3_2), .out4(D4_2), .out5(D5_2), .out6(D6_2), .out7(D7_2),
    .sel({A2, A1, A0}), .en(E));
endmodule
