// Logisim project hw3_ex3a.circ as structural Verilog: 1 circuit, main circuit main
module main (
  input  _0,
  input  _1,
  input  _2,
  input  _3,
  input  _4,
  input  _5,
  input  _6,
  input  _7,
  input  _8,
  input  _9,
  output out_11,
  output out_12,
  output out_13,
  output out_14
);

  or A (out_11, _8, _9);
  or B (out_12, _4, _5, _6, _7);
  or C (out_13, _2, _3, _6, _7);
  or D (out_14, _1, _3, _5, _7, _9);
endmodule
