// Logisim project hw3_ex3b.circ as structural Verilog: 1 circuit, main circuit main
module main (
  input  _0,
  input  A,
  input  _1,
  input  _2,
  input  _3,
  input  B,
  input  _4,
  input  _5,
  input  C,
  input  _6,
  input  _7,
  input  _8,
  input  D,
  input  _9
);

  wire a_2_out, A_nB_nC_2_out, A_nB_nC_out, A_out, b_2_out, B_out, c_2_out, C_out, d_2_out, D_out, e_out,
       f_out, g_out, nA_nB_out, nA_nBC_out, nA_nC_nD_out, nAB_nC_out, nAB_nCD_out, nAB_nD_out, nAB_out,
       nABD_out, nAC_nD_out, nAC_out, nACD_out, nAD_out, nB_nC_nD_out, not_1_out, not_2_out, not_3_out,
       not_4_out;

  or u_A (A_out, _8, _9);
  or u_B (B_out, _4, _5, _6, _7);
  or u_C (C_out, _2, _3, _6, _7);
  or u_D (D_out, _1, _3, _5, _7, _9);
  not not_1 (not_1_out, A);
  not not_2 (not_2_out, B);
  not not_3 (not_3_out, C);
  not not_4 (not_4_out, D);
  and nAC (nAC_out, not_1_out, C);
  and nABD (nABD_out, not_1_out, B, D);
  and nB_nC_nD (nB_nC_nD_out, not_2_out, not_3_out, not_4_out);
  and nA_nB (nA_nB_out, not_1_out, not_2_out);
  and nAB (nAB_out, not_1_out, B);
  and A_nB_nC (A_nB_nC_out, A, not_2_out, not_3_out);
  and nA_nC_nD (nA_nC_nD_out, not_1_out, not_3_out, not_4_out);
  and nACD (nACD_out, not_1_out, C, D);
  and A_nB_nC_2 (A_nB_nC_2_out, A, not_2_out, not_3_out);
  and nAD (nAD_out, not_1_out, D);
  and nAC_nD (nAC_nD_out, not_1_out, C, not_4_out);
  and nA_nBC (nA_nBC_out, not_1_out, not_2_out, C);
  and nAB_nC (nAB_nC_out, not_1_out, B, not_3_out);
  and nAB_nD (nAB_nD_out, not_1_out, B, not_4_out);
  and nAB_nCD (nAB_nCD_out, not_1_out, B, not_3_out, D);
  or a_2 (a_2_out, nAC_out, nABD_out, nB_nC_nD_out, A_nB_nC_out);
  or b_2 (b_2_out, nA_nB_out, nA_nC_nD_out, nACD_out, A_nB_nC_2_out);
  or c_2 (c_2_out, nAB_out, nAD_out, nB_nC_nD_out, A_nB_nC_2_out);
  or d_2 (d_2_out, nAC_nD_out, nA_nBC_out, nB_nC_nD_out, A_nB_nC_2_out, nAB_nCD_out);
  or e (e_out, nAC_nD_out, nB_nC_nD_out);
  or f (f_out, nAB_nC_out, nA_nC_nD_out, nAB_nD_out, A_nB_nC_2_out);
  or g (g_out, nAC_nD_out, nA_nBC_out, nAB_nC_out, A_nB_nC_2_out);
  _7_Segment_Display u_7_segment_display_1 (
    .g(g_out), .f(f_out), .a(a_2_out), .b(b_2_out), .e(e_out), .d(d_2_out), .c(c_2_out));  // open: dp
  // also tied to GND on the sheet: _0
endmodule
