// Logisim project hw3_ex4.circ as structural Verilog: 1 circuit, main circuit main
module main (
  input  E,
  input  D0,
  input  D1,
  input  D2,
  input  D3,
  input  D4,
  input  D5,
  input  D6,
  input  D7,
  input  in_10,
  input  in_11,
  input  in_12,
  input  D0_2,
  input  in_14,
  input  D1_2,
  input  D2_2,
  input  D3_2,
  input  D4_2,
  input  D5_2,
  input  D6_2,
  input  D7_2,
  input  in_22,
  input  in_23,
  input  in_24,
  output out_25,
  output out_26,
  output out_27
);

  wire not_1_out;

  not not_1 (not_1_out, E);
  Multiplexer #(.select(3)) multiplexer_1 (
    .in0(D0), .in1(D1), .in2(D2), .in3(D3), .in4(D4), .in5(D5), .in6(D6), .in7(D7), .out(out_25),
    .sel({in_10, in_11, in_12}), .en(not_1_out));
  Multiplexer #(.select(3)) multiplexer_2 (
    .in0(D0_2), .in1(D1_2), .in2(D2_2), .in3(D3_2), .in4(D4_2), .in5(D5_2), .in6(D6_2), .in7(D7_2),
    .out(out_27), .sel({in_22, in_23, in_24}), .en(E));
  Multiplexer #(.enable("false")) multiplexer_3 (.in0(out_25), .in1(out_27), .out(out_26), .sel(in_14));
endmodule
