// Logisim project hw3_ex5.circ as structural Verilog: 1 circuit, main circuit main
module main (
  input  PC,
  input  in_2,
  input  in_3,
  input  in_4,
  output MONITO_X,
  output PLOTTER_A,
  output PLOTTER_B,
  output LASER_PRINTER,
  output MONITOR_Y
);

  wire demultiplexer_1_out0, demultiplexer_1_out3, demultiplexer_1_out4;

  Demultiplexer #(.select(3), .enable("false")) demultiplexer_1 (
    .out0(demultiplexer_1_out0), .out1(MONITO_X), .out2(PLOTTER_A), .out3(demultiplexer_1_out3),
    .out4(demultiplexer_1_out4), .out5(PLOTTER_B), .out6(LASER_PRINTER), .out7(MONITOR_Y), .in(PC),
    .sel({in_2, in_3, in_4}));
  // also tied to GND on the sheet: {demultiplexer_1_out3, demultiplexer_1_out4, demultiplexer_1_out0}
endmodule
